// Digital circuit MMU_v1.dig as structural Verilog
module MMU_v1 (
  input  nIORQ70,
  input  Adr2,
  input  CART_ROM_SWAP
);

  wire _7474_1_p5, _7474_1_p6, _7474_1_p7, _7474_1_p8, _7474_1_p11, _7474_1_p12, _74541_1_p13, _74541_1_p14,
       _74541_1_p15, _74541_1_p16, _74541_1_p17, _74541_1_p18, _74670_1_p13, _74670_1_p14, _74670_1_p15,
       _74670_1_p16, _74670_2_p13, _74670_2_p14, _74670_2_p15, _74670_2_p16, A0_out, A1_out, A14_out,
       A15_out, D0_out, D1_out, D2_out, D3_out, D4_out, D5_out, D6_out, D7_out, nBUSACK_out, nMREQ_out,
       not_1_out, not_2_out, not_3_out, not_4_out, not_5_out, nRD_out, nRST_out, nWR_out, or_1_out, or_2_out,
       or_3_out, or_4_out, or_5_out, or_6_out, or_7_out, or_8_out;

  Button #(.activeLow("true")) nRD (.out(nRD_out));
  Button #(.activeLow("true")) nWR (.out(nWR_out));
  Button #(.activeLow("true")) nBUSACK (.out(nBUSACK_out));
  Button #(.activeLow("true")) nRST (.out(nRST_out));
  DipSwitch A14 (.out(A14_out));
  DipSwitch A15 (.out(A15_out));
  Button #(.activeLow("true")) nMREQ (.out(nMREQ_out));
  not not_1 (not_1_out, Adr2);
  or or_1 (or_1_out, not_1_out, nIORQ70);
  not not_2 (not_2_out, nBUSACK_out);
  not not_3 (not_3_out, nRST_out);
  or or_2 (or_2_out, nIORQ70, Adr2);
  or or_3 (or_3_out, or_2_out, nWR_out);
  or or_4 (or_4_out, or_1_out, nWR_out);
  or or_5 (or_5_out, not_2_out, not_3_out);
  not not_4 (not_4_out, or_5_out);
  // _7474 _7474_1: pin names not known; wires that end beside it: 1'b1, 1'b1, or_4_out, not_4_out, _7474_1_p5, _7474_1_p6, _7474_1_p7, _7474_1_p8, 1'b1, 1'b0, _7474_1_p11, _7474_1_p12
  // NotConnected on _7474_1_p5
  // NotConnected on _7474_1_p6
  // NotConnected on _7474_1_p7
  // NotConnected on _7474_1_p8
  DipSwitch D0 (.out(D0_out));
  DipSwitch D1 (.out(D1_out));
  DipSwitch D2 (.out(D2_out));
  DipSwitch D3 (.out(D3_out));
  DipSwitch A0 (.out(A0_out));
  DipSwitch A1 (.out(A1_out));
  DipSwitch D4 (.out(D4_out));
  DipSwitch D5 (.out(D5_out));
  DipSwitch D6 (.out(D6_out));
  DipSwitch D7 (.out(D7_out));
  LED led_1 (.in(_7474_1_p11));
  LED led_2 (.in(_7474_1_p12));
  // _74670 _74670_1: pin names not known; wires that end beside it: D0_out, D1_out, D2_out, D3_out, or_3_out, A0_out, A1_out, A14_out, A15_out, _7474_1_p12, 1'b1, 1'b0, _74670_1_p13, _74670_1_p14, _74670_1_p15, _74670_1_p16
  // _74670 _74670_2: pin names not known; wires that end beside it: D4_out, D5_out, D6_out, D7_out, or_3_out, A0_out, A1_out, A14_out, A15_out, _7474_1_p12, 1'b1, 1'b0, _74670_2_p13, _74670_2_p14, _74670_2_p15, _74670_2_p16
  PullDown pulldown_1 (.out(_74670_2_p13));
  PullDown pulldown_2 (.out(_74670_2_p16));
  PullDown pulldown_3 (.out(_74670_2_p14));
  PullDown pulldown_4 (.out(_74670_2_p15));
  not not_5 (not_5_out, _74670_2_p16);
  // _74541 _74541_1: pin names not known; wires that end beside it: 1'b1, 1'b0, or_2_out, nRD_out, _74670_1_p13, _74670_1_p14, _74670_1_p15, _74670_1_p16, _74670_2_p13, _74670_2_p14, _74670_2_p15, _74670_2_p16, _74541_1_p13, _74541_1_p14, _74541_1_p15, _74541_1_p16, _74541_1_p17, _74541_1_p18
  PullDown pulldown_5 (.out(_74670_1_p16));
  PullDown pulldown_6 (.out(_74670_1_p15));
  PullDown pulldown_7 (.out(_74670_1_p14));
  PullDown pulldown_8 (.out(_74670_1_p13));
  or or_6 (or_6_out, _74670_2_p16, nMREQ_out);
  or or_7 (or_7_out, not_5_out, nMREQ_out);
  LED eAddr14 (.in(_74670_1_p13));
  LED eAddr15 (.in(_74670_1_p14));
  LED eAddr16 (.in(_74670_1_p15));
  LED eAddr17 (.in(_74670_1_p16));
  LED eAddr18 (.in(_74670_2_p13));
  LED led_3 (.in(_74670_2_p14));
  LED led_4 (.in(_74670_2_p15));
  LED led_5 (.in(_74670_2_p16));
  LED nCE_RAM (.in(or_7_out));
  LED Data0 (.in(_74541_1_p13));
  LED Data1 (.in(_74541_1_p14));
  LED Data2 (.in(_74541_1_p15));
  LED Data3 (.in(_74541_1_p16));
  LED Data4 (.in(_74541_1_p17));
  LED nROM_RAM (.in(_74541_1_p18));
  or or_8 (or_8_out, CART_ROM_SWAP, or_6_out);
  LED nCE_ROM_MB (.in(or_8_out));
  LED nCE_ROM_CART (.in(or_6_out));

  // Notes on the sheet:
  //   nIORQ70: default 1
endmodule
