// Digital circuit kbd led latch.dig as structural Verilog
module kbd_led_latch (
  input  PIO_1,
  input  PIO_2
);

  wire _7474_1_pin6, _7474_1_pin8, nRESET_out, PIO_CLK_out;

  Button #(.activeLow("true")) nRESET (.out(nRESET_out));
  Button PIO_CLK (.out(PIO_CLK_out));
  _7474 _7474_1 (
    .pin1(nRESET_out), .pin2(PIO_1), .pin3(PIO_CLK_out), .pin4(1'b1), .pin6(_7474_1_pin6), .pin7(1'b0),
    .pin8(_7474_1_pin8), .pin10(1'b1), .pin11(PIO_CLK_out), .pin12(PIO_2), .pin13(nRESET_out), .pin14(1'b1));  // open: pin5, pin9
  // PolarityAwareLED polarityawareled_1: pin names not known; wires that end beside it: 1'b1, _7474_1_pin8
  // PolarityAwareLED polarityawareled_2: pin names not known; wires that end beside it: 1'b1, _7474_1_pin6
endmodule
